# Fritzing sketch crs_fritzing (saved by Fritzing 0.9.6b)
breadboards: 1

parts:
  Componente2 = Bluetooth HC-05 Macho
  Display1 = LCD screen 16x2 IIC [part_number=101290]
  Componente1 = Arduino Uno (Rev3) - ICSP
  TD-er1 = MH-Z19 CO2 sensor [part_number=MH-Z19]
  DS1 = DS18B20 1-Wire Temperature Sensor Probe Cable
  R2 = Resistor [tolerance=±5% resistance=4.7k package="0402 [SMD]"]
  Capacitive_Soil_Moisture_Sensor1 = DFRobot Capacitive Soil Moisture Sensor V1.0 [part_number=SEN0193]
  S1 = Pushbutton [package="[THT]"]

nets:
  N1: Componente2.TXD, Componente1.D0/RX
  N2: Componente2.RXD, Componente1.D1/TX
  VCC: Componente2.VCC, Display1.VCC, TD-er1.Vin, DS1.VDD, Capacitive_Soil_Moisture_Sensor1.VCC
  GND: Componente2.GND, Display1.GND, Componente1.GND, TD-er1.GND, DS1.GND, Capacitive_Soil_Moisture_Sensor1.GND, S1.Pin_1, S1.Pin_2
  N3: Display1.SDA, Componente1.A4/SDA
  N4: Display1.SCL, Componente1.A5/SCL
  N5: Componente1.A0, Capacitive_Soil_Moisture_Sensor1.A
  N6: Componente1.D10_PWM/SS, TD-er1.TX
  N7: Componente1.D11_PWM/MOSI, TD-er1.RX
  N8: Componente1.D13/SCK, S1.Pin_3, S1.Pin_4
  N9: Componente1.D2, R2.Pin_0
  N10: DS1.shield, R2.Pin_1

custom parts:
  LCD screen 16x2 IIC: LCD screen with HD44780 controller enables showing text, symbols, value or anything else that comes from Croduino/Arduino. It is capable of showing 16 symbols in two lines and therefore can be used in many projects that need to send clearly visible and legible output information.. • Color of symbols: White • Backlight: Blue • Dimensions: 80 x 36 x 12 mm • Screen dimensions: 64.5 x 16 mm •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
  DFRobot Capacitive Soil Moisture Sensor V1.0: DFRobot Capacitive Soil Moisture Sensor V1.0 This product measures soil moisture levels by capacitive sensing, rather than resistive sensing like other types of moisture sensor. It is made of a corrosion resistant material giving it a long service life. Insert it into soil and impress your friends with the real-time soil moisture data! The product includes an on-board voltage regulator which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
